# Fritzing sketch raspberrypiweatherstation (saved by Fritzing 0.9.2b)

parts:
  Raspberry_Pi1 = Raspberry Pi B+
  U1 = RJ45 Jack [package=rj45-8]
  U2 = RJ45 Jack [package=rj45-8]
  U3 = RJ45 Jack [package=rj45-8]
  U4 = RJ45 Jack [package=rj45-8]  # not connected
  U5 = SUP500F [package=sup500f]
  BMP1 = BMP085 Breakout
  IC1 = MCP3008 8-channel 10-bit ADC [part_number=MCP3008]
  Part1 = Humidity Sensor - HIH-4030 Breakout
  S1 = SWITCH-MOMENTARY-2 [package=reed_switch_pth]
  S2 = SWITCH-MOMENTARY-2 [package=reed_switch_pth]
  S3 = SWITCH-MOMENTARY-2 [package=reed_switch_pth]
  S4 = SWITCH-MOMENTARY-2 [package=reed_switch_pth]
  S5 = SWITCH-MOMENTARY-2 [package=reed_switch_pth]
  S6 = SWITCH-MOMENTARY-2 [package=reed_switch_pth]
  S7 = SWITCH-MOMENTARY-2 [package=reed_switch_pth]
  S8 = SWITCH-MOMENTARY-2 [package=reed_switch_pth]
  S9 = SWITCH-MOMENTARY-2 [package=reed_switch_pth]
  S10 = SWITCH-MOMENTARY-2 [package=reed_switch_pth]
  R1 = Resistor [tolerance=±5% resistance=33k package="0805 [SMD]"]
  R2 = Resistor [tolerance=±5% resistance=8.2k package="0805 [SMD]"]
  R3 = Resistor [tolerance=±5% resistance=1k package="0805 [SMD]"]
  R4 = Resistor [tolerance=±5% resistance=2.2k package="0805 [SMD]"]
  R5 = Resistor [tolerance=±5% resistance=3.9k package="0805 [SMD]"]
  R6 = Resistor [tolerance=±5% resistance=16k package="0805 [SMD]"]
  R7 = Resistor [tolerance=±5% resistance=120k package="0805 [SMD]"]
  R8 = Resistor [tolerance=±5% resistance=64.9k package="0805 [SMD]"]
  R9 = Resistor [tolerance=±5% resistance=220 package="0805 [SMD]"]
  R10 = Resistor [tolerance=±5% resistance=220 package="0805 [SMD]"]
  R11 = PHOTOCELL [package=photocell]  # not connected

nets (from the breadboard view):
  3V3: Raspberry_Pi1.3v3, Raspberry_Pi1.3V3, U1.1, U2.2
  GND: Raspberry_Pi1.GND, U1.2, U1.6, U2.7, U5.GND
  N1: Raspberry_Pi1.GPIO10, U2.3
  N2: Raspberry_Pi1.GPIO9, U2.6
  N3: Raspberry_Pi1.GPIO11, U2.4
  N4: Raspberry_Pi1.GPIO26, U1.5
  N5: Raspberry_Pi1.GPIO21, U1.7
  N6: Raspberry_Pi1.GPIO20, U1.4
  N7: Raspberry_Pi1.GPIO16, U1.3
  N8: Raspberry_Pi1.GPIO8, U2.1
  N9: Raspberry_Pi1.GPIO24, U2.8
  N10: Raspberry_Pi1.GPIO23, U2.5
  N11: Raspberry_Pi1.GPIO15, U5.TX-O
  N12: Raspberry_Pi1.5V, U1.8, U5.PSEL
  N13: U3.7, BMP1.VIN
  N14: IC1.no_name_yet#1, Part1.OUT
  N15: S1.1, R1.Pin_1
  N16: S1.2, S2.2, S3.2, S4.2, S5.2, S6.2, S7.2, S8.2
  N17: S2.1, R2.Pin_0
  N18: S3.1, R3.Pin_1
  N19: S4.1, R4.Pin_1
  N20: S5.1, R5.Pin_1
  N21: S6.1, R6.Pin_0
  N22: S7.1, R7.Pin_0
  N23: S8.1, R8.Pin_0
  N24: S9.2, R9.Pin_0
  N25: S10.2, R10.Pin_0
  N26: R1.Pin_0, R2.Pin_1, R3.Pin_0, R4.Pin_0, R5.Pin_0, R6.Pin_1, R7.Pin_1, R8.Pin_1

custom parts:
  BMP085 Breakout: A breakout for the BMP085 barometric pressure and temperature sensor
