# Fritzing sketch StationCircuitBoards (saved by Fritzing 0.9.3b)
circuit board: 10.16cm x 6.35cm
circuit board: 7.62cm x 3.81cm
breadboards: 1

parts:
  DHT1 = DHT11 Humitidy and Temperature Sensor
  BMP183 = Adafruit BMP183
  J2 = female pin header, 4 pins [form="♀ (female)" part_number=1]
  J3 = female pin header, 4 pins [form="♀ (female)" part_number=1]
  Raspberry_Pi_1 = Raspberry Pi 3 [part_number=RPI-3-V1.2]
  R1 = Resistor [tolerance=±5% resistance=10k package=THT]
  DS1 = DS18B20 1-Wire Temperature Sensor [part_number=DS18B20]
  R2 = Resistor [tolerance=±5% resistance=4.7k package=THT]
  Part1 = Soil Moisture Sensor
  IC1 = MCP3008 8-channel 10-bit ADC [part_number=MCP3008]
  J4 = RJ9 [package=rj9]
  J5 = RJ9 [package=rj9]
  R4 = PHOTOCELL [package=photocell-kit]
  R5 = Resistor [tolerance=±5% resistance=10k package=THT]

nets (from the schematic view):
  VDD: DHT1.VDD, BMP183.VIN, J2.pin1, J3.pin1, Raspberry_Pi_1.5V, R1.Pin_0, J4.1
  N1: DHT1.DATA, Raspberry_Pi_1.GIPO5, R1.Pin_1
  GND: DHT1.GND, BMP183.GND, J2.pin4, J3.pin4, Raspberry_Pi_1.GND, DS1.GND, Part1.GND, IC1.no_name_yet#9, IC1.no_name_yet#14, J4.3, J5.3, R4.P$2
  N2: BMP183.SCK, Raspberry_Pi_1.GIPO6
  N3: BMP183.SDO, Raspberry_Pi_1.GIPO12
  N4: BMP183.SDI, Raspberry_Pi_1.GIPO16
  N5: BMP183.CS, Raspberry_Pi_1.GIPO13
  N6: J2.pin3, IC1.no_name_yet#1
  N7: J3.pin3, IC1.no_name_yet#2
  3V3: Raspberry_Pi_1.3v3, Raspberry_Pi_1.3V3, DS1.VDD, R2.Pin_1, Part1.VCC, IC1.no_name_yet#15, IC1.no_name_yet#16, R5.Pin_0
  N8: Raspberry_Pi_1.GIPO4, DS1.DQ, R2.Pin_0
  N9: Raspberry_Pi_1.GIPO10, IC1.no_name_yet#11
  N10: Raspberry_Pi_1.GIPO9, IC1.no_name_yet#12
  N11: Raspberry_Pi_1.GIPO11, IC1.no_name_yet#13
  N12: Raspberry_Pi_1.GIPO26, J4.2
  N13: Raspberry_Pi_1.GIPO21, J5.2
  N14: Raspberry_Pi_1.GIPO8, IC1.no_name_yet#10
  N15: Part1.SIG, IC1.no_name_yet#3
  N16: IC1.no_name_yet#4, J4.4
  N17: R4.P$1, R5.Pin_1

notes:
  GND
  5V
  Gas2
  Gas1
  DHT
  SCk
  SDO
  SDI
  CS
  3.3V
  Soil
  CLK
  DOUT
  DIN
  Wind Dir
  Weather v2.0
  Spaceman

custom parts:
  DHT11 Humitidy and Temperature Sensor: DHT11 Humidity and Temperature Sensor
  Adafruit BMP183: Fans of the BMP085/BMP180 will want to take a look at the new BMP183 - an SPI spin on the old familiar classic. This precision sensor from Bosch is the best low-cost sensing solution for measuring barometric pressure and temperature. Because pressure changes with altitude you can also use it as an altimeter! The BMP183 is the next-generation of sensors from Bosch, and is the fraternal twin of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
